// Logisim project 1.circ as structural Verilog: 1 circuit, main circuit main
module main (
  input  x,
  input  y,
  input  z,
  output out
);

  wire and_1_out, and_2_out, and_3_out;

  and and_1 (and_1_out, y, x);
  and and_2 (and_2_out, z, x);
  and and_3 (and_3_out, y, y);
  or or_1 (out, and_3_out, and_1_out, and_2_out, and_2_out, and_2_out);
endmodule
