// Logisim project hw0ex1.circ as structural Verilog: 1 circuit, main circuit main
module main (
  input  c1,
  input  c0,
  output d11,
  output d10,
  output d01,
  output out_6
);

  wire not_1_out, not_2_out, not_3_out, not_4_out;

  buf and_1 (d10, c1);  // AND_Gate
  not not_1 (not_1_out, c0);
  // AND_Gate and_2 has open pins: out=d11
  not not_2 (not_2_out, c1);
  // AND_Gate and_3 has open pins: out=d01
  not not_3 (not_3_out, c0);
  not not_4 (not_4_out, c1);
  // AND_Gate and_4 has open pins: out=out_6
endmodule
