// Logisim project hw0ex2.circ as structural Verilog: 1 circuit, main circuit main
module main (
  input  x2,
  input  x1,
  input  x0,
  input  y2,
  input  y1,
  input  y0,
  output out_7
);

  wire xor_1_out;

  xor xor_1 (xor_1_out, x0, y0);
  not not_1 (out_7, xor_1_out);
endmodule
