// Logisim project hw2q1.circ as structural Verilog: 1 circuit, main circuit main
module main (
  input  x0,
  input  x1,
  input  x2,
  input  x3,
  input  y0,
  input  y1,
  input  y2,
  input  y3,
  input  zx,
  input  nx,
  input  zy,
  input  ny,
  input  f,
  input  no,
  output out_15,
  output out_16,
  output out_17,
  output out_18
);

  wire adder_1_cout, adder_1_out, adder_2_cout, adder_2_out, adder_3_cout, adder_3_out, adder_4_out,
       and_1_out, and_2_out, and_3_out, and_4_out, and_5_out, and_6_out, and_7_out, and_8_out, and_9_out,
       and_10_out, and_11_out, and_12_out, and_13_out, and_14_out, and_15_out, and_16_out, and_17_out,
       and_18_out, and_19_out, and_20_out, not_1_out, not_2_out, not_3_out, or_1_out, or_2_out, or_3_out,
       or_4_out, xor_1_out, xor_2_out, xor_3_out, xor_4_out, xor_5_out, xor_6_out, xor_7_out, xor_8_out;

  not not_1 (not_1_out, zx);
  not not_2 (not_2_out, zy);
  and and_1 (and_1_out, x0, not_1_out);
  and and_2 (and_2_out, x1, not_1_out);
  and and_3 (and_3_out, x2, not_1_out);
  and and_4 (and_4_out, x3, not_1_out);
  and and_5 (and_5_out, y0, not_2_out);
  and and_6 (and_6_out, y1, not_2_out);
  and and_7 (and_7_out, not_2_out, y2);
  and and_8 (and_8_out, y3, not_2_out);
  xor xor_1 (xor_1_out, nx, and_1_out);
  xor xor_2 (xor_2_out, nx, and_2_out);
  xor xor_3 (xor_3_out, nx, and_3_out);
  xor xor_4 (xor_4_out, nx, and_4_out);
  xor xor_5 (xor_5_out, and_5_out, ny);
  xor xor_6 (xor_6_out, and_6_out, ny);
  xor xor_7 (xor_7_out, and_7_out, ny);
  xor xor_8 (xor_8_out, and_8_out, ny);
  Adder #(.width(1)) adder_1 (.a(xor_1_out), .b(xor_5_out), .out(adder_1_out), .cin(1'b0), .cout(adder_1_cout));
  Adder #(.width(1)) adder_2 (.a(xor_2_out), .b(xor_6_out), .out(adder_2_out), .cin(adder_1_cout), .cout(adder_2_cout));
  Adder #(.width(1)) adder_3 (.a(xor_3_out), .b(xor_7_out), .out(adder_3_out), .cin(adder_2_cout), .cout(adder_3_cout));
  Adder #(.width(1)) adder_4 (.a(xor_4_out), .b(xor_8_out), .out(adder_4_out), .cin(adder_3_cout));  // open: cout
  and and_9 (and_9_out, xor_1_out, xor_5_out);
  and and_10 (and_10_out, xor_2_out, xor_6_out);
  and and_11 (and_11_out, xor_3_out, xor_7_out);
  and and_12 (and_12_out, xor_4_out, xor_8_out);
  not not_3 (not_3_out, f);
  and and_13 (and_13_out, adder_1_out, f);
  and and_14 (and_14_out, adder_2_out, f);
  and and_15 (and_15_out, adder_3_out, f);
  and and_16 (and_16_out, adder_4_out, f);
  and and_17 (and_17_out, and_9_out, not_3_out);
  and and_18 (and_18_out, and_10_out, not_3_out);
  and and_19 (and_19_out, and_11_out, not_3_out);
  and and_20 (and_20_out, and_12_out, not_3_out);
  or or_1 (or_1_out, and_13_out, and_17_out);
  or or_2 (or_2_out, and_14_out, and_18_out);
  or or_3 (or_3_out, and_15_out, and_19_out);
  or or_4 (or_4_out, and_16_out, and_20_out);
  xor xor_9 (out_15, or_1_out, no);
  xor xor_10 (out_16, or_2_out, no);
  xor xor_11 (out_17, or_3_out, no);
  xor xor_12 (out_18, or_4_out, no);

  // Notes on the sheet:
  //   ALU Serafima Nerush
endmodule
