// Logisim project hw3.circ as structural Verilog: 3 circuits, main circuit main
module main (
  input  \input ,
  input  clear,
  output just_saw_101_e262e305
);

  wire clock_1_out;
  wire [1:0] next_1_o0, register_1_q;

  next next_1 (.\input (\input ), .s1(register_1_q[1]), .s0(register_1_q[0]), .O1(next_1_o0[1]), .O0(next_1_o0[0]));
  Clock clock_1 (.out(clock_1_out));
  Register #(.width(2)) register_1 (.D(next_1_o0), .en(1'b1), .clk(clock_1_out), .Q(register_1_q), .clr(clear));
  out out_1 (.s1(register_1_q[1]), .s0(register_1_q[0]), .\output (just_saw_101_e262e305));

  // Notes on the sheet:
  //   Serafima Nerush (logisim evolution)
endmodule

module next (
  input  \input ,
  input  s1,
  input  s0,
  output O1,
  output O0
);

  wire and_1_out, and_2_out, and_4_out, not_1_out, not_2_out, not_3_out, or_1_out;

  not not_1 (not_1_out, \input );
  not not_2 (not_2_out, s1);
  not not_3 (not_3_out, s0);
  and and_1 (and_1_out, s0, not_2_out);
  and and_2 (and_2_out, not_2_out, not_1_out, s0);
  and and_3 (O0, \input , or_1_out);
  or or_1 (or_1_out, not_3_out, and_1_out);
  and and_4 (and_4_out, s1, \input , not_3_out);
  or or_2 (O1, and_2_out, and_4_out);
endmodule

module out (
  input  s1,
  input  s0,
  output \output 
);

  and and_1 (\output , s1, s0);
endmodule
