// Logisim project lab2ex1ex2ex3.circ as structural Verilog: 4 circuits, main circuit fourbit_neg
module fourbit_neg (
  input  a3,
  input  a2,
  input  a1,
  input  a0,
  output z3,
  output z2,
  output z1,
  output z0
);

  wire adder_2_cout, adder_3_cout, adder_4_cout, not_1_out, not_2_out, not_3_out, not_4_out;

  not not_1 (not_1_out, a3);
  Adder #(.width(1)) adder_1 (.a(not_1_out), .b(adder_2_cout), .out(z3));  // open: cin, cout
  not not_2 (not_2_out, a2);
  Adder #(.width(1)) adder_2 (.a(not_2_out), .b(adder_3_cout), .out(z2), .cout(adder_2_cout));  // open: cin
  not not_3 (not_3_out, a0);
  not not_4 (not_4_out, a1);
  Adder #(.width(1)) adder_3 (.a(not_4_out), .b(adder_4_cout), .out(z1), .cout(adder_3_cout));  // open: cin
  Adder #(.width(1)) adder_4 (.a(not_3_out), .b(1'b1), .out(z0), .cout(adder_4_cout));  // open: cin

  // Notes on the sheet:
  //   Lab 2 ex 1 Serafima Nerush (NOTE: logisim-evolution)
endmodule

module cinFA (
  input  cin,
  input  x,
  input  y,
  output sum,
  output cout
);

  wire and_1_out, and_2_out, and_3_out, and_4_out, xor_1_out;

  and and_1 (and_1_out, y, x);
  and and_2 (and_2_out, x, cin);
  or or_1 (cout, and_1_out, and_2_out, and_3_out);
  ExactlyOne xor_1 (.out(xor_1_out), .in0(cin), .in1(x), .in2(y));
  and and_3 (and_3_out, y, cin);
  and and_4 (and_4_out, cin, x, y);
  or or_2 (sum, xor_1_out, and_4_out);
endmodule

module substractor (
  input  a0,
  input  a1,
  input  a2,
  input  a3,
  input  b0,
  input  b1,
  input  b2,
  input  b3,
  output c0,
  output c1,
  output c2,
  output c3,
  output overflow
);

  wire cinfa_1_cout, cinfa_2_cout, cinfa_3_cout, fourbit_neg_1_z0, fourbit_neg_1_z1, fourbit_neg_1_z2,
       fourbit_neg_1_z3;

  fourbit_neg fourbit_neg_1 (
    .a3(b3), .a2(b2), .a1(b1), .a0(b0), .z3(fourbit_neg_1_z3), .z2(fourbit_neg_1_z2), .z1(fourbit_neg_1_z1),
    .z0(fourbit_neg_1_z0));
  cinFA cinfa_1 (.cin(1'b0), .x(a0), .y(fourbit_neg_1_z0), .sum(c0), .cout(cinfa_1_cout));
  cinFA cinfa_2 (.cin(cinfa_1_cout), .x(a1), .y(fourbit_neg_1_z1), .sum(c1), .cout(cinfa_2_cout));
  cinFA cinfa_3 (.cin(cinfa_2_cout), .x(a2), .y(fourbit_neg_1_z2), .sum(c2), .cout(cinfa_3_cout));
  cinFA cinfa_4 (.cin(cinfa_3_cout), .x(a3), .y(fourbit_neg_1_z3), .sum(c3), .cout(overflow));

  // Notes on the sheet:
  //   Substraction Serafima Nerush (logisim-evolution)
endmodule

module comparison (
  input  in_1,
  input  in_2,
  input  in_3,
  input  in_4,
  input  in_5,
  input  in_6,
  input  in_7,
  input  in_8,
  output out_9
);

  wire or_1_out, substractor_1_c0, substractor_1_c1, substractor_1_c2, substractor_1_c3;

  substractor substractor_1 (
    .a0(in_1), .a1(in_2), .a2(in_3), .a3(in_4), .b0(in_5), .b1(in_6), .b2(in_7), .b3(in_8),
    .c0(substractor_1_c0), .c1(substractor_1_c1), .c2(substractor_1_c2), .c3(substractor_1_c3));  // open: overflow
  or or_1 (or_1_out, substractor_1_c0, substractor_1_c1, substractor_1_c2, substractor_1_c3);
  not not_1 (out_9, or_1_out);

  // Notes on the sheet:
  //   comparator Serafima Nerush
endmodule
