// Logisim project mux4.circ as structural Verilog: 1 circuit, main circuit main
module main (
  input  line00,
  input  line01,
  input  line_10,
  input  line_11,
  input  select0,
  input  select1,
  output out_7
);

  wire and_1_out, and_2_out, and_3_out, and_4_out, not_1_out, not_2_out;

  not not_1 (not_1_out, select0);
  not not_2 (not_2_out, select1);
  and and_1 (and_1_out, select0, not_2_out, line_10);
  and and_2 (and_2_out, line01, select1, not_1_out);
  and and_3 (and_3_out, line_11, select0, select1);
  and and_4 (and_4_out, not_1_out, line00, not_2_out);
  or or_1 (out_7, and_2_out, and_4_out, and_1_out, and_3_out);

  // Notes on the sheet:
  //   MUX 4:1 Serafima Nerush
endmodule
