// Logisim project parity.circ as structural Verilog: 1 circuit, main circuit main
module main (
  input  x,
  input  y,
  input  z,
  output out_4
);

  wire and_1_out, and_2_out, and_3_out, not_1_out, not_2_out, or_1_out, or_2_out;

  or or_1 (or_1_out, x, y);
  not not_1 (not_1_out, and_1_out);
  and and_1 (and_1_out, x, y);
  and and_2 (and_2_out, or_1_out, not_1_out);
  or or_2 (or_2_out, and_2_out, z);
  and and_3 (and_3_out, and_2_out, z);
  not not_2 (not_2_out, and_3_out);
  and and_4 (out_4, or_2_out, not_2_out);

  // Notes on the sheet:
  //   Parity Serafima Nerush
endmodule
