// Logisim project saturate2.circ as structural Verilog: 3 circuits, main circuit main
module main (
  input  down,
  input  clear
);

  wire clock_1_out, out_1_bot, out_1_lbot, out_1_ltop, out_1_out_6, out_1_rbot, out_1_rtop, out_1_top;
  wire [1:0] next_1_out_5, register_1_q;

  Register #(.width(2)) register_1 (.D(next_1_out_5), .en(1'b1), .clk(clock_1_out), .Q(register_1_q), .clr(clear));
  next next_1 (.d(down), .q1(register_1_q[1]), .q0(register_1_q[0]), .out_4(next_1_out_5[1]), .out_5(next_1_out_5[0]));
  Clock clock_1 (.out(clock_1_out));
  out out_1 (
    .q1(register_1_q[1]), .q0(register_1_q[0]), .top(out_1_top), .ltop(out_1_ltop), .rtop(out_1_rtop),
    .out_6(out_1_out_6), .lbot(out_1_lbot), .rbot(out_1_rbot), .bot(out_1_bot));
  _7_Segment_Display u_7_segment_display_1 (
    .g(out_1_out_6), .f(out_1_ltop), .a(out_1_top), .b(out_1_rtop), .e(out_1_lbot), .d(out_1_bot),
    .c(out_1_rbot));  // open: dp

  // Notes on the sheet:
  //   Serafima Nerush (logisim-evolution)
endmodule

module next (
  input  d,
  input  q1,
  input  q0,
  output out_4,
  output out_5
);

  wire and_1_out, and_2_out, and_3_out, and_4_out, and_5_out, and_6_out, and_7_out, not_1_out, not_2_out,
       not_3_out, not_4_out, not_5_out, not_6_out, not_7_out, not_8_out, or_1_out, or_2_out, xor_1_out;

  not not_1 (not_1_out, d);
  and and_1 (and_1_out, not_1_out, q1, q0);
  not not_2 (not_2_out, d);
  xor xor_1 (xor_1_out, q1, q0);
  not not_3 (not_3_out, q0);
  not not_4 (not_4_out, d);
  and and_2 (and_2_out, q0, q1);
  not not_5 (not_5_out, q0);
  and and_3 (and_3_out, not_2_out, xor_1_out);
  and and_4 (and_4_out, not_3_out, not_4_out);
  and and_5 (and_5_out, and_2_out, d);
  and and_6 (and_6_out, not_5_out, d);
  not not_6 (not_6_out, q0);
  not not_7 (not_7_out, q1);
  and and_7 (and_7_out, not_6_out, not_7_out, d);
  not not_8 (not_8_out, and_7_out);
  or or_1 (or_1_out, and_4_out, and_1_out, and_6_out);
  or or_2 (or_2_out, and_1_out, and_3_out, and_5_out);
  and and_8 (out_4, or_2_out, not_8_out);
  and and_9 (out_5, or_1_out, not_8_out);
endmodule

module out (
  input  q1,
  input  q0,
  output top,
  output ltop,
  output rtop,
  output out_6,
  output lbot,
  output rbot,
  output bot
);

  wire and_2_out, and_3_out, not_1_out, not_2_out, not_3_out, not_4_out;

  not not_1 (not_1_out, q1);
  not not_2 (not_2_out, q0);
  not not_3 (not_3_out, q1);
  not not_4 (not_4_out, q0);
  and and_1 (ltop, not_1_out, not_2_out);
  and and_2 (and_2_out, not_3_out, q0);
  not not_5 (bot, and_2_out);
  not not_6 (lbot, q0);
  and and_3 (and_3_out, q1, not_4_out);
  not not_7 (rbot, and_3_out);

  assign out_6 = q1;
  assign rtop = 1'b1;
  assign top = bot;
endmodule
